// Logisim project 202255663 설종환.circ as structural Verilog: 11 circuits, main circuit main
module main (
);

  wire alu_1_zero, clock_1_out, controlunit_1_alusrc, controlunit_1_memwrite, controlunit_1_pcsrc,
       controlunit_1_regwrite, Reset_out;
  wire [1:0] controlunit_1_resultsrc, ImmSrc;
  wire [2:0] controlunit_1_alucontorl;
  wire [31:0] adder_1_out, adder_2_out, alu_1_out_4, datamemory_1_rd, immgen_1_b_type, immgen_1_i_type,
       immgen_1_j_type, immgen_1_s_type, multiplexer_1_out, multiplexer_2_out, multiplexer_3_out,
       multiplexer_4_out, register_1_q, registerfile_1_rd1, registerfile_1_rd1_2, rom_1_data;

  Multiplexer #(.width(32)) multiplexer_1 (
    .in0(adder_1_out), .in1(adder_2_out), .out(multiplexer_1_out), .sel(controlunit_1_pcsrc));  // open: en
  Clock clock_1 (.out(clock_1_out));
  Register #(.width(32)) register_1 (
    .D(multiplexer_1_out), .Q(register_1_q), .clk(clock_1_out), .clr(Reset_out));  // open: en
  Button Reset (.out(Reset_out));
  Adder #(.width(32)) adder_1 (.a(register_1_q), .b(32'h4), .out(adder_1_out));  // open: cin, cout
  ROM #(.addrWidth(6), .dataWidth(32)) rom_1 (.addr(register_1_q[7:2]), .data(rom_1_data));  // open: sel
  // Probe on rom_1_data[6:0]
  ImmGen immgen_1 (
    .Instruction(rom_1_data), .S_type(immgen_1_s_type), .B_type(immgen_1_b_type), .J_type(immgen_1_j_type),
    .I_type(immgen_1_i_type));
  ControlUnit controlunit_1 (
    .Zero(alu_1_zero), .Opcode(rom_1_data[6:0]), .Func3(rom_1_data[14:12]), .Func7(rom_1_data[30]),
    .PCSrc(controlunit_1_pcsrc), .ResultSrc(controlunit_1_resultsrc), .MemWrite(controlunit_1_memwrite),
    .ALUSrc(controlunit_1_alusrc), .ImmSrc(ImmSrc), .RegWrite(controlunit_1_regwrite),
    .ALUContorl(controlunit_1_alucontorl));
  // Probe on registerfile_1_rd1
  // Probe on rom_1_data[19:15]
  RegisterFile registerfile_1 (
    .WE3(controlunit_1_regwrite), .A1(rom_1_data[19:15]), .A2(rom_1_data[24:20]), .A3(rom_1_data[11:7]),
    .WD3(multiplexer_4_out), .RD1(registerfile_1_rd1), .RD1_2(registerfile_1_rd1_2), .CLK(clock_1_out));
  // Probe on rom_1_data[24:20]
  // Probe on rom_1_data[11:7]
  Multiplexer #(.select(2), .width(32)) multiplexer_2 (
    .in0(immgen_1_i_type), .in1(immgen_1_b_type), .in2(immgen_1_s_type), .in3(immgen_1_j_type),
    .out(multiplexer_2_out), .sel(ImmSrc));  // open: en
  Multiplexer #(.width(32)) multiplexer_3 (
    .in0(registerfile_1_rd1_2), .in1(multiplexer_2_out), .out(multiplexer_3_out), .sel(controlunit_1_alusrc));  // open: en
  Adder #(.width(32)) adder_2 (.a(multiplexer_2_out), .b(register_1_q), .out(adder_2_out));  // open: cin, cout
  ALU alu_1 (
    .out_4(alu_1_out_4), .Zero(alu_1_zero), .in_1(registerfile_1_rd1), .in_2(multiplexer_3_out),
    .ALU_Control(controlunit_1_alucontorl));
  // Probe on multiplexer_3_out
  DataMemory datamemory_1 (
    .A(alu_1_out_4[9:2]), .WD(registerfile_1_rd1_2), .RD(datamemory_1_rd), .CLK(clock_1_out),
    .WE(controlunit_1_memwrite));
  Multiplexer #(.select(2), .width(32)) multiplexer_4 (
    .in0(alu_1_out_4), .in1(datamemory_1_rd), .in2(adder_1_out), .out(multiplexer_4_out),
    .sel(controlunit_1_resultsrc));  // open: in3, en
  // Probe on multiplexer_4_out

  // Notes on the sheet:
  //   PC
  //   과제의 명령어가 이미
  //   들어가 있습니다
  //   Inst Mem
  //   contents of rom_1 (hex, n*v repeats v):
  //   493 100413 6500293 20545863 8484b3 141413 ff5ff06f 902423 802903 940433 1240433 540433 40433
  //   PCTarget
  //   or
  //   Imm
  //   ALUResult
  //   or
  //   RD
  //   or
  //   PC+4
endmodule

module ALU (
  input  [31:0] in_1,
  input  [31:0] in_2,
  input  [2:0] ALU_Control,
  output [31:0] out_4,
  output Zero
);

  wire comparator_1_eq, comparator_1_gt, or_1_out;
  wire [31:0] adder_1_out, multiplexer_1_out, shifter_1_out;

  Adder #(.width(32)) adder_1 (.a(in_1), .b(in_2), .out(adder_1_out));  // open: cin, cout
  Shifter #(.width(32)) shifter_1 (.in(in_1), .\dist (in_2[4:0]), .out(shifter_1_out));
  Comparator #(.width(32)) comparator_1 (.a(in_1), .b(in_2), .gt(comparator_1_gt), .eq(comparator_1_eq));  // open: lt
  or or_1 (or_1_out, comparator_1_eq, comparator_1_gt);
  Multiplexer #(.width(32), .enable("false")) multiplexer_1 (
    .in0({32{1'b0}}), .in1(32'h1), .out(multiplexer_1_out), .sel(or_1_out));
  Multiplexer #(.select(3), .width(32), .disabled(0), .enable("false")) multiplexer_2 (
    .in0(adder_1_out), .in1(multiplexer_1_out), .in2(adder_1_out), .in3(shifter_1_out), .out(out_4),
    .sel(ALU_Control));  // open: in4, in5, in6, in7
  Bit_Extender #(.in_width(32), .out_width(1)) bit_extender_1 (.in(multiplexer_1_out), .out(Zero));

  // Notes on the sheet:
  //   A
  //   B
  //   ADD,ADDI
  //   SLLI
  //   BGE
  //   Output
endmodule

module RegisterFile (
  input  WE3,
  input  CLK,
  input  [4:0] A1,
  input  [4:0] A2,
  input  [4:0] A3,
  input  [31:0] WD3,
  output [31:0] RD1,
  output [31:0] RD1_2
);

  wire demultiplexer_1_out0, demultiplexer_1_out1;
  wire [31:0] rf16_1_rd1, rf16_1_rd2, rf16_2_rd1, rf16_2_rd2;

  Demultiplexer demultiplexer_1 (
    .out0(demultiplexer_1_out0), .out1(demultiplexer_1_out1), .in(WE3), .sel(A3[4]));  // open: en
  RF16 rf16_1 (
    .WE(demultiplexer_1_out0), .A1(A1[3:0]), .A2(A2[3:0]), .A3(A3[3:0]), .WD3(WD3), .RD1(rf16_1_rd1),
    .RD2(rf16_1_rd2), .CLK(CLK));
  RF16 rf16_2 (
    .WE(demultiplexer_1_out1), .A1(A1[3:0]), .A2(A2[3:0]), .A3(A3[3:0]), .WD3(WD3), .RD1(rf16_2_rd1),
    .RD2(rf16_2_rd2), .CLK(CLK));
  Multiplexer #(.width(32)) multiplexer_1 (.in0(rf16_1_rd1), .in1(rf16_2_rd1), .out(RD1), .sel(A1[4]));  // open: en
  Multiplexer #(.width(32)) multiplexer_2 (.in0(rf16_1_rd2), .in1(rf16_2_rd2), .out(RD1_2), .sel(A2[4]));  // open: en
endmodule

module RF4 (
  input  CLK,
  input  [1:0] A1,
  input  WE,
  input  [1:0] A3,
  input  [1:0] A2,
  input  [31:0] WD3,
  output [31:0] RD1,
  output [31:0] RD2
);

  wire demultiplexer_1_out0, demultiplexer_1_out1, demultiplexer_1_out2, demultiplexer_1_out3;
  wire [31:0] register_1_q, register_2_q, register_3_q, register_4_q;

  Demultiplexer #(.select(2)) demultiplexer_1 (
    .out0(demultiplexer_1_out0), .out1(demultiplexer_1_out1), .out2(demultiplexer_1_out2),
    .out3(demultiplexer_1_out3), .in(WE), .sel(A3));  // open: en
  Register #(.width(32)) register_1 (.D(WD3), .en(demultiplexer_1_out0), .Q(register_1_q), .clk(CLK));  // open: clr
  Register #(.width(32)) register_2 (.D(WD3), .en(demultiplexer_1_out1), .Q(register_2_q), .clk(CLK));  // open: clr
  Register #(.width(32)) register_3 (.D(WD3), .en(demultiplexer_1_out2), .Q(register_3_q), .clk(CLK));  // open: clr
  Register #(.width(32)) register_4 (.D(WD3), .en(demultiplexer_1_out3), .Q(register_4_q), .clk(CLK));  // open: clr
  Multiplexer #(.select(2), .width(32)) multiplexer_1 (
    .in0(register_1_q), .in1(register_2_q), .in2(register_3_q), .out(RD1), .sel(A1));  // open: in3, en
  Multiplexer #(.select(2), .width(32)) multiplexer_2 (
    .in0(register_1_q), .in1(register_2_q), .in2(register_3_q), .in3(register_4_q), .out(RD2), .sel(A2));  // open: en
endmodule

module RF16 (
  input  CLK,
  input  WE,
  input  [3:0] A1,
  input  [3:0] A2,
  input  [3:0] A3,
  input  [31:0] WD3,
  output [31:0] RD1,
  output [31:0] RD2
);

  wire demultiplexer_1_out0, demultiplexer_1_out1, demultiplexer_1_out2, demultiplexer_1_out3;
  wire [31:0] rf4_1_rd1, rf4_1_rd2, rf4_2_rd1, rf4_2_rd2, rf4_3_rd1, rf4_3_rd2, rf4_4_rd1, rf4_4_rd2;

  Demultiplexer #(.select(2)) demultiplexer_1 (
    .out0(demultiplexer_1_out0), .out1(demultiplexer_1_out1), .out2(demultiplexer_1_out2),
    .out3(demultiplexer_1_out3), .in(WE), .sel(A3[3:2]));  // open: en
  RF4 rf4_1 (
    .WE(demultiplexer_1_out0), .WD3(WD3), .RD1(rf4_1_rd1), .RD2(rf4_1_rd2), .CLK(CLK), .A3(A3[1:0]),
    .A1(A1[1:0]), .A2(A2[1:0]));
  RF4 rf4_2 (
    .WE(demultiplexer_1_out1), .WD3(WD3), .RD1(rf4_2_rd1), .RD2(rf4_2_rd2), .CLK(CLK), .A3(A3[1:0]),
    .A1(A1[1:0]), .A2(A2[1:0]));
  RF4 rf4_3 (
    .WE(demultiplexer_1_out2), .WD3(WD3), .RD1(rf4_3_rd1), .RD2(rf4_3_rd2), .CLK(CLK), .A3(A3[1:0]),
    .A1(A1[1:0]), .A2(A2[1:0]));
  RF4 rf4_4 (
    .WE(demultiplexer_1_out3), .WD3(WD3), .RD1(rf4_4_rd1), .RD2(rf4_4_rd2), .CLK(CLK), .A3(A3[1:0]),
    .A1(A1[1:0]), .A2(A2[1:0]));
  Multiplexer #(.select(2), .width(32)) multiplexer_1 (
    .in0(rf4_1_rd1), .in1(rf4_2_rd1), .in2(rf4_3_rd1), .in3(rf4_4_rd1), .out(RD1), .sel(A1[3:2]));  // open: en
  Multiplexer #(.select(2), .width(32)) multiplexer_2 (
    .in0(rf4_1_rd2), .in1(rf4_2_rd2), .in2(rf4_3_rd2), .in3(rf4_4_rd2), .out(RD2), .sel(A2[3:2]));  // open: en

  // Other names for the same wires on the sheet: A1U[1:0] = A1[3:2]; A2U[1:0] = A2[3:2]; A3U[1:0] = A3[3:2]
endmodule

module DataMemory (
  input  [7:0] A,
  input  CLK,
  input  WE,
  input  [31:0] WD,
  output [31:0] RD
);

  wire not_1_out;

  RAM #(.dataWidth(32)) ram_1 (.addr(A), .data(RD), .clk(CLK), .ld(not_1_out));  // open: sel, clr
  not not_1 (not_1_out, WE);
  assign RD = WE ? WD : 32'bz;  // Controlled_Buffer controlled_buffer_1

  // Notes on the sheet:
  //   Data Memory
endmodule

module ImmGen (
  input  [31:0] Instruction,
  output [31:0] I_type,
  output [31:0] S_type,
  output [31:0] B_type,
  output [31:0] J_type
);

  assign I_type = {{20{Instruction[31]}}, Instruction[31:20]};  // Bit_Extender bit_extender_1
  assign S_type = {{20{Instruction[31]}}, {Instruction[31:25], Instruction[11:7]}};  // Bit_Extender bit_extender_2
  assign B_type = {{19{Instruction[31]}}, {Instruction[31], Instruction[7], Instruction[30:25], Instruction[11:8], 1'b0}};  // Bit_Extender bit_extender_3
  assign J_type = {{11{Instruction[31]}}, {Instruction[31], Instruction[19:12], Instruction[20], Instruction[30:21], 1'b0}};  // Bit_Extender bit_extender_4
endmodule

module InsTypeDecoder (
  input  [6:0] Opcode,
  output R_type,
  output lw,
  output sw,
  output Branch,
  output I_Type,
  output jal
);

  Comparator #(.width(7), .mode("unsigned")) comparator_1 (.a(7'b0110011), .b(Opcode), .eq(R_type));  // open: gt, lt
  Comparator #(.width(7), .mode("unsigned")) comparator_2 (.a(Opcode), .b(7'b0000011), .eq(lw));  // open: gt, lt
  Comparator #(.width(7), .mode("unsigned")) comparator_3 (.a(Opcode), .b(7'b0100011), .eq(sw));  // open: gt, lt
  Comparator #(.width(7), .mode("unsigned")) comparator_4 (.a(Opcode), .b(7'b1100011), .eq(Branch));  // open: gt, lt
  Comparator #(.width(7), .mode("unsigned")) comparator_5 (.a(Opcode), .b(7'b0010011), .eq(I_Type));  // open: gt, lt
  Comparator #(.width(7), .mode("unsigned")) comparator_6 (.a(Opcode), .b(7'b1101111), .eq(jal));  // open: gt, lt
endmodule

module ALUDecoder (
  input  [1:0] ALUOp,
  input  OP_5,
  input  [2:0] Func_3,
  input  Func7,
  output [2:0] ALUControl
);

  wire [2:0] multiplexer_1_out;

  Multiplexer #(.width(3)) multiplexer_1 (
    .in0(3'b010), .in1(3'b011), .out(multiplexer_1_out), .sel(Func_3[0]), .en(ALUOp[1]));
  Multiplexer #(.select(2), .width(3)) multiplexer_2 (
    .in0(3'b000), .in1(3'b001), .in2(multiplexer_1_out), .out(ALUControl), .sel(ALUOp));  // open: in3, en
endmodule

module MainDecoder (
  input  R_Type,
  input  lw,
  input  sw,
  input  Branch,
  input  l_Type,
  input  jal,
  output Branch_2,
  output Jump,
  output [1:0] ResultSrc,
  output MemWrite,
  output ALUSrc,
  output [1:0] ImmSrc,
  output RegWrite,
  output [1:0] ALUOP
);

  wire or_1_out, or_2_out, or_3_out, or_4_out;

  or or_1 (or_1_out, R_Type, l_Type);
  or or_2 (or_2_out, lw, l_Type);
  or or_3 (or_3_out, lw, sw);
  or or_4 (or_4_out, l_Type, R_Type);
  Priority_Encoder #(.select(2)) priority_encoder_1 (
    .in0(or_1_out), .in1(lw), .in2(jal), .out(ResultSrc));  // open: in3, gs, en_out, en_in
  or or_5 (ALUSrc, lw, sw, l_Type);
  Priority_Encoder #(.select(2)) priority_encoder_2 (
    .in0(or_2_out), .in1(sw), .in2(Branch), .in3(jal), .out(ImmSrc));  // open: gs, en_out, en_in
  or or_6 (RegWrite, R_Type, lw, l_Type);
  Priority_Encoder #(.select(2)) priority_encoder_3 (
    .in0(or_3_out), .in1(Branch), .in2(or_4_out), .out(ALUOP));  // open: in3, gs, en_out, en_in

  assign Branch_2 = Branch;
  assign Jump = jal;
  assign MemWrite = sw;
endmodule

module ControlUnit (
  input  Zero,
  input  [6:0] Opcode,
  input  [2:0] Func3,
  input  Func7,
  output PCSrc,
  output [1:0] ResultSrc,
  output MemWrite,
  output ALUSrc,
  output [1:0] ImmSrc,
  output RegWrite,
  output [2:0] ALUContorl
);

  wire and_1_out, instypedecoder_1_branch, instypedecoder_1_i_type, instypedecoder_1_jal,
       instypedecoder_1_lw, instypedecoder_1_r_type, instypedecoder_1_sw, maindecoder_1_branch_2,
       maindecoder_1_jump;
  wire [1:0] maindecoder_1_aluop;
  wire [4:4] undriven;

  InsTypeDecoder instypedecoder_1 (
    .Opcode(Opcode), .R_type(instypedecoder_1_r_type), .lw(instypedecoder_1_lw), .sw(instypedecoder_1_sw),
    .Branch(instypedecoder_1_branch), .I_Type(instypedecoder_1_i_type), .jal(instypedecoder_1_jal));
  MainDecoder maindecoder_1 (
    .Branch_2(maindecoder_1_branch_2), .Jump(maindecoder_1_jump), .ResultSrc(ResultSrc), .MemWrite(MemWrite),
    .ALUSrc(ALUSrc), .ImmSrc(ImmSrc), .RegWrite(RegWrite), .ALUOP(maindecoder_1_aluop),
    .R_Type(instypedecoder_1_r_type), .lw(instypedecoder_1_lw), .sw(instypedecoder_1_sw),
    .Branch(instypedecoder_1_branch), .l_Type(instypedecoder_1_i_type), .jal(instypedecoder_1_jal));
  ALUDecoder aludecoder_1 (
    .ALUControl(ALUContorl), .ALUOp(maindecoder_1_aluop), .OP_5(undriven[4]), .Func_3(Func3), .Func7(Func7));
  and and_1 (and_1_out, Zero, maindecoder_1_branch_2);
  or or_1 (PCSrc, and_1_out, maindecoder_1_jump);
endmodule
