// Logisim project ALU.circ as structural Verilog: 1 circuit, main circuit main
module main (
  input  [31:0] in_1,
  input  [31:0] in_2,
  input  [2:0] ALU_Control,
  output [31:0] out_4,
  output Zero
);

  wire comparator_1_eq, comparator_1_gt, or_1_out;
  wire [31:0] adder_1_out, multiplexer_1_out, shifter_1_out;

  Adder #(.width(32)) adder_1 (.a(in_1), .b(in_2), .out(adder_1_out));  // open: cin, cout
  Shifter #(.width(32)) shifter_1 (.in(in_1), .\dist (in_2[4:0]), .out(shifter_1_out));
  Comparator #(.width(32)) comparator_1 (.a(in_1), .b(in_2), .gt(comparator_1_gt), .eq(comparator_1_eq));  // open: lt
  or or_1 (or_1_out, comparator_1_eq, comparator_1_gt);
  Multiplexer #(.width(32), .enable("false")) multiplexer_1 (
    .in0({32{1'b0}}), .in1(32'h1), .out(multiplexer_1_out), .sel(or_1_out));
  Multiplexer #(.select(3), .width(32), .disabled(0), .enable("false")) multiplexer_2 (
    .in0(adder_1_out), .in1(multiplexer_1_out), .in2(adder_1_out), .in3(shifter_1_out), .out(out_4),
    .sel(ALU_Control));  // open: in4, in5, in6, in7
  Bit_Extender #(.in_width(32), .out_width(1)) bit_extender_1 (.in(multiplexer_1_out), .out(Zero));

  // Notes on the sheet:
  //   A
  //   B
  //   ADD,ADDI
  //   SLLI
  //   BGE
  //   Output
endmodule
