// Logisim project ALUDecoder.circ as structural Verilog: 1 circuit, main circuit main
module main (
  input  [1:0] ALUOp,
  input  OP_5,
  input  [2:0] Func_3,
  input  Func7,
  output [2:0] ALUControl
);

  wire [2:0] multiplexer_1_out;

  Multiplexer #(.width(3)) multiplexer_1 (
    .in0(3'b010), .in1(3'b011), .out(multiplexer_1_out), .sel(Func_3[0]), .en(ALUOp[1]));
  Multiplexer #(.select(2), .width(3)) multiplexer_2 (
    .in0(3'b000), .in1(3'b001), .in2(multiplexer_1_out), .out(ALUControl), .sel(ALUOp));  // open: in3, en
endmodule
