// Logisim project ALUOp.circ as structural Verilog: 1 circuit, main circuit main
module main (
  input  lw,
  input  sw,
  input  R_Type,
  input  I_Type,
  input  B_type,
  output [1:0] out_6
);

  wire and_1_out, nor_1_out, not_1_out, or_1_out;
  wire [1:0] and_2_out;

  nor nor_1 (nor_1_out, lw, sw);
  or or_1 (or_1_out, R_Type, I_Type);
  not not_1 (not_1_out, or_1_out);
  and and_1 (and_1_out, nor_1_out, or_1_out);
  and and_2 (and_2_out[0], not_1_out, nor_1_out);
  or or_2 (and_2_out[1], nor_1_out, and_1_out);
  Multiplexer #(.width(2)) multiplexer_1 (.in0(and_2_out), .in1(2'b01), .out(out_6), .sel(B_type));  // open: en
endmodule
