// Logisim project ControlUnit.circ as structural Verilog: 1 circuit, main circuit main
module main (
  input  Zero,
  input  [6:0] Opcode,
  input  [2:0] Func3,
  input  Func7,
  output PCSrc,
  output [1:0] ResultSrc,
  output MemWrite,
  output ALUSrc,
  output [1:0] ImmSrc,
  output RegWrite,
  output [2:0] ALUContorl
);

  wire and_1_out, main_1_branch, main_1_i_type, main_1_jal, main_1_lw, main_1_r_type, main_1_sw,
       main_2_branch_2, main_2_jump;
  wire [1:0] main_2_aluop;

  InsTypeDecoder_main main_1 (
    .Opcode(Opcode), .R_type(main_1_r_type), .lw(main_1_lw), .sw(main_1_sw), .Branch(main_1_branch),
    .I_Type(main_1_i_type), .jal(main_1_jal));
  MainDecoder_main main_2 (
    .Branch_2(main_2_branch_2), .Jump(main_2_jump), .ResultSrc(ResultSrc), .MemWrite(MemWrite),
    .ALUSrc(ALUSrc), .ImmSrc(ImmSrc), .RegWrite(RegWrite), .ALUOP(main_2_aluop), .R_Type(main_1_r_type),
    .Load(main_1_lw), .Store(main_1_sw), .Branch(main_1_branch), .l_Type(main_1_i_type), .JAL(main_1_jal));
  ALUDecoder_main main_3 (
    .ALUControl(ALUContorl), .ALUOp(main_2_aluop), .OP_5(Opcode[4]), .Func7(Func7), .Func_3(Func3));
  and and_1 (and_1_out, Zero, main_2_branch_2);
  or or_1 (PCSrc, and_1_out, main_2_jump);
endmodule
