// Logisim project DataMemory.circ as structural Verilog: 1 circuit, main circuit main
module main (
  input  [7:0] A,
  input  CLK,
  input  WE,
  input  [31:0] WD,
  output [31:0] RD
);

  wire not_1_out;

  RAM #(.dataWidth(32)) ram_1 (.addr(A), .data(RD), .clk(CLK), .ld(not_1_out));  // open: sel, clr
  not not_1 (not_1_out, WE);
  assign RD = WE ? WD : 32'bz;  // Controlled_Buffer controlled_buffer_1

  // Notes on the sheet:
  //   Data Memory
endmodule
