// Logisim project ImmGen.circ as structural Verilog: 1 circuit, main circuit main
module main (
  input  [31:0] Instruction,
  output [31:0] S_type,
  output [31:0] B_type,
  output [31:0] J_type,
  output [31:0] I_type
);

  assign S_type = {{20{Instruction[31]}}, {Instruction[31:25], Instruction[11:7]}};  // Bit_Extender bit_extender_1
  assign B_type = {{19{Instruction[31]}}, {Instruction[31], Instruction[7], Instruction[30:25], Instruction[11:8], 1'b0}};  // Bit_Extender bit_extender_2
  assign J_type = {{11{Instruction[31]}}, {Instruction[31], Instruction[19:12], Instruction[20], Instruction[30:21], 1'b0}};  // Bit_Extender bit_extender_3
  assign I_type = {{20{Instruction[31]}}, Instruction[31:20]};  // Bit_Extender bit_extender_4
endmodule
