// Logisim project InsTypeDecoder.circ as structural Verilog: 1 circuit, main circuit main
module main (
  input  [6:0] Opcode,
  output R_type,
  output lw,
  output sw,
  output Branch,
  output I_Type,
  output jal
);

  Comparator #(.width(7), .mode("unsigned")) comparator_1 (.a(7'b0110011), .b(Opcode), .eq(R_type));  // open: gt, lt
  Comparator #(.width(7), .mode("unsigned")) comparator_2 (.a(Opcode), .b(7'b0000011), .eq(lw));  // open: gt, lt
  Comparator #(.width(7), .mode("unsigned")) comparator_3 (.a(Opcode), .b(7'b0100011), .eq(sw));  // open: gt, lt
  Comparator #(.width(7), .mode("unsigned")) comparator_4 (.a(Opcode), .b(7'b1100011), .eq(Branch));  // open: gt, lt
  Comparator #(.width(7), .mode("unsigned")) comparator_5 (.a(Opcode), .b(7'b0010011), .eq(I_Type));  // open: gt, lt
  Comparator #(.width(7), .mode("unsigned")) comparator_6 (.a(Opcode), .b(7'b1101111), .eq(jal));  // open: gt, lt
endmodule
