// Logisim project MainDecoder.circ as structural Verilog: 1 circuit, main circuit main
module main (
  input  R_Type,
  input  Load,
  input  Store,
  input  Branch,
  input  l_Type,
  input  JAL,
  output Branch_2,
  output Jump,
  output [1:0] ResultSrc,
  output MemWrite,
  output ALUSrc,
  output [1:0] ImmSrc,
  output RegWrite,
  output [1:0] ALUOP
);

  wire or_1_out, or_2_out, or_3_out, or_4_out;

  or or_1 (or_1_out, R_Type, l_Type);
  or or_2 (or_2_out, Load, l_Type);
  or or_3 (or_3_out, Load, Store);
  or or_4 (or_4_out, l_Type, R_Type);
  Priority_Encoder #(.select(2)) priority_encoder_1 (
    .in0(or_1_out), .in1(Load), .in2(JAL), .out(ResultSrc));  // open: in3, gs, en_out, en_in
  or or_5 (ALUSrc, Load, Store, l_Type);
  Priority_Encoder #(.select(2)) priority_encoder_2 (
    .in0(or_2_out), .in1(Store), .in2(Branch), .in3(JAL), .out(ImmSrc));  // open: gs, en_out, en_in
  or or_6 (RegWrite, R_Type, Load, l_Type);
  Priority_Encoder #(.select(2)) priority_encoder_3 (
    .in0(or_3_out), .in1(Branch), .in2(or_4_out), .out(ALUOP));  // open: in3, gs, en_out, en_in

  assign Branch_2 = Branch;
  assign Jump = JAL;
  assign MemWrite = Store;
endmodule
