// Logisim project RF16.circ as structural Verilog: 1 circuit, main circuit main
module main (
  input  CLK,
  input  WE,
  input  [3:0] A1,
  input  [3:0] A2,
  input  [3:0] A3,
  input  [31:0] WD3,
  output [31:0] RD1,
  output [31:0] RD2
);

  wire demultiplexer_1_out0, demultiplexer_1_out1, demultiplexer_1_out2, demultiplexer_1_out3;
  wire [31:0] main_1_rd1, main_1_rd2, main_2_rd1, main_2_rd2, main_3_rd1, main_3_rd2, main_4_rd1, main_4_rd2;

  Demultiplexer #(.select(2)) demultiplexer_1 (
    .out0(demultiplexer_1_out0), .out1(demultiplexer_1_out1), .out2(demultiplexer_1_out2),
    .out3(demultiplexer_1_out3), .in(WE), .sel(A3[3:2]));  // open: en
  RF4_main main_1 (
    .WE(demultiplexer_1_out0), .WD3(WD3), .RD1(main_1_rd1), .RD2(main_1_rd2), .CLK(CLK), .A3(A3[1:0]),
    .A1(A1[1:0]), .A2(A2[1:0]));
  RF4_main main_2 (
    .WE(demultiplexer_1_out1), .WD3(WD3), .RD1(main_2_rd1), .RD2(main_2_rd2), .CLK(CLK), .A3(A3[1:0]),
    .A1(A1[1:0]), .A2(A2[1:0]));
  RF4_main main_3 (
    .WE(demultiplexer_1_out2), .WD3(WD3), .RD1(main_3_rd1), .RD2(main_3_rd2), .CLK(CLK), .A3(A3[1:0]),
    .A1(A1[1:0]), .A2(A2[1:0]));
  RF4_main main_4 (
    .WE(demultiplexer_1_out3), .WD3(WD3), .RD1(main_4_rd1), .RD2(main_4_rd2), .CLK(CLK), .A3(A3[1:0]),
    .A1(A1[1:0]), .A2(A2[1:0]));
  Multiplexer #(.select(2), .width(32)) multiplexer_1 (
    .in0(main_1_rd1), .in1(main_2_rd1), .in2(main_3_rd1), .in3(main_4_rd1), .out(RD1), .sel(A1[3:2]));  // open: en
  Multiplexer #(.select(2), .width(32)) multiplexer_2 (
    .in0(main_1_rd2), .in1(main_2_rd2), .in2(main_3_rd2), .in3(main_4_rd2), .out(RD2), .sel(A2[3:2]));  // open: en

  // Other names for the same wires on the sheet: A1U[1:0] = A1[3:2]; A2U[1:0] = A2[3:2]; A3U[1:0] = A3[3:2]
endmodule
