// Logisim project RF4.circ as structural Verilog: 1 circuit, main circuit main
module main (
  input  CLK,
  input  [1:0] A1,
  input  WE,
  input  [1:0] A3,
  input  [1:0] A2,
  input  [31:0] WD3,
  output [31:0] RD1,
  output [31:0] RD2
);

  wire demultiplexer_1_out0, demultiplexer_1_out1, demultiplexer_1_out2, demultiplexer_1_out3;
  wire [31:0] register_1_q, register_2_q, register_3_q, register_4_q;

  Demultiplexer #(.select(2)) demultiplexer_1 (
    .out0(demultiplexer_1_out0), .out1(demultiplexer_1_out1), .out2(demultiplexer_1_out2),
    .out3(demultiplexer_1_out3), .in(WE), .sel(A3));  // open: en
  Register #(.width(32)) register_1 (.D(WD3), .en(demultiplexer_1_out0), .Q(register_1_q), .clk(CLK));  // open: clr
  Register #(.width(32)) register_2 (.D(WD3), .en(demultiplexer_1_out1), .Q(register_2_q), .clk(CLK));  // open: clr
  Register #(.width(32)) register_3 (.D(WD3), .en(demultiplexer_1_out2), .Q(register_3_q), .clk(CLK));  // open: clr
  Register #(.width(32)) register_4 (.D(WD3), .en(demultiplexer_1_out3), .Q(register_4_q), .clk(CLK));  // open: clr
  Multiplexer #(.select(2), .width(32)) multiplexer_1 (
    .in0(register_1_q), .in1(register_2_q), .in2(register_3_q), .out(RD1), .sel(A1));  // open: in3, en
  Multiplexer #(.select(2), .width(32)) multiplexer_2 (
    .in0(register_1_q), .in1(register_2_q), .in2(register_3_q), .in3(register_4_q), .out(RD2), .sel(A2));  // open: en
endmodule
