// Logisim project RegisterFile.circ as structural Verilog: 1 circuit, main circuit main
module main (
  input  WE3,
  input  CLK,
  input  [4:0] A1,
  input  [4:0] A2,
  input  [4:0] A3,
  input  [31:0] WD3,
  output [31:0] RD1,
  output [31:0] RD1_2
);

  wire demultiplexer_1_out0, demultiplexer_1_out1;
  wire [31:0] main_1_rd1, main_1_rd2, main_2_rd1, main_2_rd2;

  Demultiplexer demultiplexer_1 (
    .out0(demultiplexer_1_out0), .out1(demultiplexer_1_out1), .in(WE3), .sel(A3[4]));  // open: en
  RF16_main main_1 (
    .WE(demultiplexer_1_out0), .A1(A1[3:0]), .A2(A2[3:0]), .A3(A3[3:0]), .WD3(WD3), .RD1(main_1_rd1),
    .RD2(main_1_rd2), .CLK(CLK));
  RF16_main main_2 (
    .WE(demultiplexer_1_out1), .A1(A1[3:0]), .A2(A2[3:0]), .A3(A3[3:0]), .WD3(WD3), .RD1(main_2_rd1),
    .RD2(main_2_rd2), .CLK(CLK));
  Multiplexer #(.width(32)) multiplexer_1 (.in0(main_1_rd1), .in1(main_2_rd1), .out(RD1), .sel(A1[4]));  // open: en
  Multiplexer #(.width(32)) multiplexer_2 (.in0(main_1_rd2), .in1(main_2_rd2), .out(RD1_2), .sel(A2[4]));  // open: en
endmodule
